// Logisim project display-4bits-c2.circ as structural Verilog: 1 circuit, main circuit main
module main (
  input  b3,
  input  b2,
  input  b1,
  input  b0,
  output s,
  output a,
  output b,
  output c,
  output d,
  output e,
  output f,
  output g
);

  wire adder_1_cout, adder_1_out, adder_2_cout, adder_2_out, adder_3_cout, adder_3_out, adder_4_out,
       xor_1_out, xor_2_out, xor_3_out, xor_4_out;

  xor xor_1 (xor_1_out, b3, b0);
  xor xor_2 (xor_2_out, b3, b1);
  xor xor_3 (xor_3_out, b3, b2);
  xor xor_4 (xor_4_out, b3, b3);
  Adder #(.width(1)) adder_1 (.a(xor_1_out), .b(1'b0), .out(adder_1_out), .cin(b3), .cout(adder_1_cout));
  Adder #(.width(1)) adder_2 (.a(xor_2_out), .b(1'b0), .out(adder_2_out), .cin(adder_1_cout), .cout(adder_2_cout));
  Adder #(.width(1)) adder_3 (.a(xor_3_out), .b(1'b0), .out(adder_3_out), .cin(adder_2_cout), .cout(adder_3_cout));
  Adder #(.width(1)) adder_4 (.a(xor_4_out), .b(1'b0), .out(adder_4_out), .cin(adder_3_cout));  // open: cout
  _7_Segment_Display u_7_segment_display_1 (.g(g), .f(f), .a(a), .b(b), .e(e), .d(d), .c(c));  // open: dp
  // _7_Segment_Display 7_segment_display_2: pin names not known; wires that end beside it: adder_2_out, adder_1_out, adder_4_out, b3, a
  // _7_segment_display_driver 7_segment_display_driver_1: pin names not known; wires that end beside it: b3, b2, b2, b1, b1, b0, b0, adder_4_out, adder_4_out, adder_3_out, adder_3_out, adder_2_out, adder_1_out, adder_3_out, adder_2_out, adder_1_out, b, c, d, e, f, g

  assign s = b3;
endmodule
