// Logisim project binario-bcd.circ as structural Verilog: 1 circuit, main circuit main
module main (
  input  b4,
  input  b3,
  input  b2,
  input  b1,
  output out_5,
  output out_6,
  output out_7,
  output out_8
);

  wire and_1_out, and_2_out, and_3_out, and_4_out, and_5_out, and_6_out, and_7_out, and_8_out, and_9_out,
       and_10_out;

  and and_1 (and_1_out, b3, b1);
  and and_2 (and_2_out, b3, b2);
  and and_3 (and_3_out, b4, b1);
  and and_4 (and_4_out, b3, ~b2, ~b1);  // AND_Gate
  and and_5 (and_5_out, b2, b1);
  and and_6 (and_6_out, b4, ~b1);  // AND_Gate
  and and_7 (and_7_out, ~b3, b2);  // AND_Gate
  and and_8 (and_8_out, ~b4, ~b3, b1);  // AND_Gate
  and and_9 (and_9_out, b3, b2, ~b1);  // AND_Gate
  and and_10 (and_10_out, b4, ~b1);  // AND_Gate
  or or_1 (out_5, and_1_out, and_2_out, b4);
  or or_2 (out_6, and_3_out, and_4_out);
  or or_3 (out_7, and_5_out, and_6_out, and_7_out);
  or or_4 (out_8, and_8_out, and_9_out, and_10_out);
endmodule
