// Logisim project comparadores.circ as structural Verilog: 4 circuits, main circuit main
module main (
  input  [3:0] in_1,
  input  [3:0] in_2
);

  wire comp_4bit_1_out_9, comp_4bit_1_out_10, comp_4bit_1_out_11;

  comp_4bit comp_4bit_1 (
    .a3(in_1[0]), .a2(in_1[1]), .a1(in_1[2]), .a0(in_1[3]), .b3(in_2[0]), .b2(in_2[1]), .b1(in_2[2]),
    .b0(in_2[3]), .out_9(comp_4bit_1_out_9), .out_10(comp_4bit_1_out_10), .out_11(comp_4bit_1_out_11));
endmodule

module comp_1bit (
  input  a,
  input  b,
  output G,
  output E,
  output L
);

  and and_1 (G, a, ~b);  // AND_Gate
  xnor xnor_1 (E, b, a);
  nor nor_1 (L, G, E);
endmodule

module comp_2bit (
  input  a1,
  input  a0,
  input  b1,
  input  b0,
  output out_5,
  output out_6,
  output out_7
);

  wire and_2_out, comp_1bit_1_e, comp_1bit_1_g, comp_1bit_2_e, comp_1bit_2_g;

  comp_1bit comp_1bit_1 (.a(a1), .b(b1), .G(comp_1bit_1_g), .E(comp_1bit_1_e));  // open: L
  comp_1bit comp_1bit_2 (.a(a0), .b(b0), .G(comp_1bit_2_g), .E(comp_1bit_2_e));  // open: L
  and and_1 (out_6, comp_1bit_1_e, comp_1bit_2_e);
  and and_2 (and_2_out, comp_1bit_1_g, comp_1bit_2_e);
  or or_1 (out_5, and_2_out, comp_1bit_2_g);
  nor nor_1 (out_7, out_6, out_5);
endmodule

module comp_4bit (
  input  a3,
  input  a2,
  input  a1,
  input  a0,
  input  b3,
  input  b2,
  input  b1,
  input  b0,
  output out_9,
  output out_10,
  output out_11
);

  wire and_2_out, comp_2bit_1_out_5, comp_2bit_1_out_6, comp_2bit_2_out_5, comp_2bit_2_out_6;

  comp_2bit comp_2bit_1 (
    .a1(a3), .b1(b3), .a0(a2), .b0(b2), .out_5(comp_2bit_1_out_5), .out_6(comp_2bit_1_out_6));  // open: out_7
  comp_2bit comp_2bit_2 (
    .a1(a1), .b1(b1), .a0(a0), .b0(b0), .out_5(comp_2bit_2_out_5), .out_6(comp_2bit_2_out_6));  // open: out_7
  and and_1 (out_10, comp_2bit_1_out_6, comp_2bit_2_out_6);
  and and_2 (and_2_out, comp_2bit_1_out_5, comp_2bit_2_out_6);
  or or_1 (out_9, and_2_out, comp_2bit_2_out_5);
  nor nor_1 (out_11, out_10, out_9);
endmodule
