// Logisim project somador-subtrator 4 bits.circ as structural Verilog: 2 circuits, main circuit main
module main (
  input  op,
  input  a3,
  input  a2,
  input  a1,
  input  a0,
  input  b3,
  input  b2,
  input  b1,
  input  b0,
  output x3,
  output x2,
  output x1,
  output x0
);

  wire n1_bit_full_adder_1_cout, n1_bit_full_adder_2_cout, n1_bit_full_adder_3_cout, xor_1_out, xor_2_out,
       xor_3_out, xor_4_out;

  xor xor_1 (xor_1_out, b0, op);
  xor xor_2 (xor_2_out, b1, op);
  xor xor_3 (xor_3_out, b2, op);
  xor xor_4 (xor_4_out, b3, op);
  _1_bit_full_adder u_1_bit_full_adder_1 (.A(a0), .B(xor_1_out), .S(x0), .Cin(op), .Cout(n1_bit_full_adder_1_cout));
  _1_bit_full_adder u_1_bit_full_adder_2 (
    .A(a1), .B(xor_2_out), .S(x1), .Cin(n1_bit_full_adder_1_cout), .Cout(n1_bit_full_adder_2_cout));
  _1_bit_full_adder u_1_bit_full_adder_3 (
    .A(a2), .B(xor_3_out), .S(x2), .Cin(n1_bit_full_adder_2_cout), .Cout(n1_bit_full_adder_3_cout));
  _1_bit_full_adder u_1_bit_full_adder_4 (.A(a3), .B(xor_4_out), .S(x3), .Cin(n1_bit_full_adder_3_cout));  // open: Cout
endmodule

module _1_bit_full_adder (
  input  Cin,
  input  A,
  input  B,
  output S,
  output Cout
);

  wire and_1_out, and_2_out, xor_1_out;

  xor xor_1 (xor_1_out, A, B);
  xor xor_2 (S, xor_1_out, Cin);
  and and_1 (and_1_out, xor_1_out, Cin);
  or or_1 (Cout, and_1_out, and_2_out);
  and and_2 (and_2_out, B, A);
endmodule
