// Logisim project somadores.circ as structural Verilog: 3 circuits, main circuit soma 4bit
module soma_4bit (
  input  Cin,
  input  a3,
  input  a2,
  input  a1,
  input  a0,
  input  b3,
  input  b2,
  input  b1,
  input  b0,
  output x3,
  output x2,
  output x1,
  output x0,
  output Cout
);

  wire soma_1bit_1_cout, soma_1bit_2_cout, soma_1bit_3_cout;

  soma_1bit soma_1bit_1 (.A(a0), .B(b0), .S(x0), .Cin(Cin), .Cout(soma_1bit_1_cout));
  soma_1bit soma_1bit_2 (.A(a1), .B(b1), .S(x1), .Cin(soma_1bit_1_cout), .Cout(soma_1bit_2_cout));
  soma_1bit soma_1bit_3 (.A(a2), .B(b2), .S(x2), .Cin(soma_1bit_2_cout), .Cout(soma_1bit_3_cout));
  soma_1bit soma_1bit_4 (.A(a3), .B(b3), .S(x3), .Cin(soma_1bit_3_cout), .Cout(Cout));
endmodule

module soma_1bit (
  input  Cin,
  input  A,
  input  B,
  output S,
  output Cout
);

  wire and_1_out, and_2_out, xor_1_out;

  xor xor_1 (xor_1_out, A, B);
  xor xor_2 (S, xor_1_out, Cin);
  and and_1 (and_1_out, xor_1_out, Cin);
  or or_1 (Cout, and_1_out, and_2_out);
  and and_2 (and_2_out, B, A);
endmodule

module soma_2bit (
  input  Cin,
  input  a1,
  input  a0,
  input  b1,
  input  b0,
  output x1,
  output x0,
  output Cout
);

  wire soma_1bit_1_cout;

  soma_1bit soma_1bit_1 (.A(a0), .B(b0), .S(x0), .Cin(Cin), .Cout(soma_1bit_1_cout));
  soma_1bit soma_1bit_2 (.A(a1), .B(b1), .S(x1), .Cin(soma_1bit_1_cout), .Cout(Cout));
endmodule
